# Fritzing sketch Untitled Sketch 5 (saved by Fritzing 0.9.3b)
breadboards: 1

parts:
  Part1 = Arduino Uno (Rev3)
  hc-sr1 = hc-sr04
  LED1 = smd LED [color="Red (633nm)" package="1206 [SMD]"]

nets:
  N1: Part1.D12/MISO, LED1.anode
  GND: Part1.GND, hc-sr1.GND, LED1.cathode
  N2: Part1.D2, hc-sr1.Echo
  N3: Part1.D3_PWM, hc-sr1.Trig
  5V: Part1.5V, hc-sr1.VCC
